// Logisim project 5 Bit CPU [1703057].circ as structural Verilog: 15 circuits, main circuit 5 Bit OR
module _5_Bit_OR (
  input  [4:0] A,
  input  [4:0] B,
  output [4:0] O
);

  or or_1 (O[4], A[4], B[4]);
  or or_2 (O[3], A[3], B[3]);
  or or_3 (O[2], A[2], B[2]);
  or or_4 (O[1], A[1], B[1]);
  or or_5 (O[0], A[0], B[0]);

  // Notes on the sheet:
  //   Roll: 1703057
endmodule

module _5_Bit_SHR (
  input  [4:0] A,
  input  [2:0] Shift,
  output [4:0] O
);

  Multiplexer #(.select(3), .enable("false")) multiplexer_1 (
    .in0(A[4]), .in1(1'b0), .in2(1'b0), .in3(1'b0), .in4(1'b0), .in5(1'b0), .in6(1'b0), .in7(1'b0),
    .out(O[4]), .sel(Shift));
  Multiplexer #(.select(3), .enable("false")) multiplexer_2 (
    .in0(A[3]), .in1(A[4]), .in2(1'b0), .in3(1'b0), .in4(1'b0), .in5(1'b0), .in6(1'b0), .in7(1'b0),
    .out(O[3]), .sel(Shift));
  Multiplexer #(.select(3), .enable("false")) multiplexer_3 (
    .in0(A[2]), .in1(A[3]), .in2(A[4]), .in3(1'b0), .in4(1'b0), .in5(1'b0), .in6(1'b0), .in7(1'b0),
    .out(O[2]), .sel(Shift));
  Multiplexer #(.select(3), .enable("false")) multiplexer_4 (
    .in0(A[1]), .in1(A[2]), .in2(A[3]), .in3(A[4]), .in4(1'b0), .in5(1'b0), .in6(1'b0), .in7(1'b0),
    .out(O[1]), .sel(Shift));
  Multiplexer #(.select(3), .enable("false")) multiplexer_5 (
    .in0(A[0]), .in1(A[1]), .in2(A[2]), .in3(A[3]), .in4(A[4]), .in5(1'b0), .in6(1'b0), .in7(1'b0),
    .out(O[0]), .sel(Shift));

  // Notes on the sheet:
  //   Roll: 1703057
endmodule

module ALU (
  input  [4:0] A__4_0,
  input  [4:0] B_4_0,
  input  OP,
  output [4:0] R__4_0,
  output ZF,
  output CF,
  output SF
);

  wire [4:0] OR, SHR;

  _5_Bit_OR u_5_bit_or_1 (.A(A__4_0), .O(OR), .B(B_4_0));
  _5_Bit_SHR u_5_bit_shr_1 (.A(A__4_0), .Shift(B_4_0[2:0]), .O(SHR));
  Multiplexer #(.width(5), .enable("false")) multiplexer_1 (.in0(OR), .in1(SHR), .out(R__4_0), .sel(OP));
  nor nor_1 (ZF, R__4_0[0], R__4_0[1], R__4_0[2], R__4_0[3], R__4_0[4]);

  assign CF = 1'b0;
  assign SF = 1'b0;

  // Other names for the same wires on the sheet: A[4:0] = A__4_0; B[4:0] = B_4_0; Sel[2:0] = B_4_0[2:0]

  // Notes on the sheet:
  //   Roll: 1703057
endmodule

module Test (
  input  [16:0] Write_Data__16_0,
  input  Write_Select,
  input  Clock,
  input  Read_Select_1,
  input  Read_Select_2,
  input  [4:0] in_6,
  input  [4:0] in_7,
  input  in_8,
  output [16:0] Read_Data_1,
  output [16:0] Read_Data_2,
  output [4:0] out_11,
  output out_12,
  output out_13,
  output out_14
);

  _1x17_SRAM u_1x17_sram_1 (
    .Write_Data__16_0(Write_Data__16_0), .Write_Select(Write_Select), .Read_Select_1(Read_Select_1),
    .Read_Select_2(Read_Select_2), .Clock(Clock), .Read_Data_1(Read_Data_1), .Read_Data_2(Read_Data_2));
  ALU alu_1 (.A__4_0(in_6), .B_4_0(in_7), .OP(in_8), .R__4_0(out_11), .CF(out_12), .SF(out_13), .ZF(out_14));

  // Other names for the same wires on the sheet: CLK = Clock; RS1 = Read_Select_1; RS2 = Read_Select_2;
  //   WS = Write_Select

  // Notes on the sheet:
  //   Roll: 1703057
endmodule

module _1_bit_Register (
  input  Din,
  input  Sel,
  input  Clock,
  output Dout
);

  wire multiplexer_1_out;

  Multiplexer #(.enable("false")) multiplexer_1 (.in0(Dout), .in1(Din), .out(multiplexer_1_out), .sel(Sel));
  D_Flip_Flop d_ff_1 (.clk(Clock), .D(multiplexer_1_out), .Q(Dout));  // open: Qn, preset, en, reset

  // Notes on the sheet:
  //   Roll: 1703057
endmodule

module _5_bit_Register (
  input  [4:0] Din_4_0,
  input  Sel,
  input  Clock,
  output [4:0] Dout_4_0
);

  // Register_Set_Library_1_bit_Register 1_bit_register_1: pin names not known; wires that end beside it: Din_4_0[4], Sel, Clock, Dout_4_0[4]
  // Register_Set_Library_1_bit_Register 1_bit_register_2: pin names not known; wires that end beside it: Din_4_0[3], Sel, Clock, Dout_4_0[3]
  // Register_Set_Library_1_bit_Register 1_bit_register_3: pin names not known; wires that end beside it: Din_4_0[2], Sel, Clock, Dout_4_0[2]
  // Register_Set_Library_1_bit_Register 1_bit_register_4: pin names not known; wires that end beside it: Din_4_0[1], Sel, Clock, Dout_4_0[1]
  // Register_Set_Library_1_bit_Register 1_bit_register_5: pin names not known; wires that end beside it: Din_4_0[0], Sel, Clock, Dout_4_0[0]

  // Notes on the sheet:
  //   Roll: 1703057
endmodule

module Register_Set_with_5_5_bit_Registers (
  input  WE,
  input  [2:0] Wr,
  input  [4:0] Wrd,
  input  Clock,
  input  [2:0] Ra,
  input  [2:0] Rb,
  output [4:0] A,
  output [4:0] B
);

  wire decoder_1_out0, decoder_1_out1, decoder_1_out2, decoder_1_out3, decoder_1_out4;
  wire [4:0] R0, R1, R2, R3, R4;

  Decoder #(.select(3)) decoder_1 (
    .out0(decoder_1_out0), .out1(decoder_1_out1), .out2(decoder_1_out2), .out3(decoder_1_out3),
    .out4(decoder_1_out4), .sel(Wr), .en(WE));  // open: out5, out6, out7
  _5_bit_Register u_5_bit_register_1 (.Din_4_0(Wrd), .Sel(decoder_1_out0), .Dout_4_0(R0), .Clock(Clock));
  _5_bit_Register u_5_bit_register_2 (.Din_4_0(Wrd), .Sel(decoder_1_out1), .Dout_4_0(R1), .Clock(Clock));
  _5_bit_Register u_5_bit_register_3 (.Din_4_0(Wrd), .Sel(decoder_1_out2), .Dout_4_0(R2), .Clock(Clock));
  _5_bit_Register u_5_bit_register_4 (.Din_4_0(Wrd), .Sel(decoder_1_out3), .Dout_4_0(R3), .Clock(Clock));
  _5_bit_Register u_5_bit_register_5 (.Din_4_0(Wrd), .Sel(decoder_1_out4), .Dout_4_0(R4), .Clock(Clock));
  Multiplexer #(.select(3), .width(5), .enable("false")) multiplexer_1 (
    .in0(R0), .in1(R1), .in2(R2), .in3(R3), .in4(R4), .out(A), .sel(Ra));  // open: in5, in6, in7
  Multiplexer #(.select(3), .width(5), .enable("false")) multiplexer_2 (
    .in0(R0), .in1(R1), .in2(R2), .in3(R3), .in4(R4), .out(B), .sel(Rb));  // open: in5, in6, in7

  // Notes on the sheet:
  //   Roll: 1703057
endmodule

module _1x1_SRAM (
  input  Read_Select_1,
  input  Read_Select_2,
  input  Write_Data,
  input  Write_Select,
  input  Clock,
  output Read_Data_1,
  output Read_Data_2
);

  wire d_ff_1_q, multiplexer_1_out;

  Multiplexer #(.enable("false")) multiplexer_1 (
    .in0(d_ff_1_q), .in1(Write_Data), .out(multiplexer_1_out), .sel(Write_Select));
  D_Flip_Flop d_ff_1 (.clk(Clock), .D(multiplexer_1_out), .Q(d_ff_1_q));  // open: Qn, preset, en, reset
  and and_1 (Read_Data_1, Read_Select_1, d_ff_1_q);
  and and_2 (Read_Data_2, Read_Select_2, d_ff_1_q);

  // Notes on the sheet:
  //   Roll: 1703057
endmodule

module _1x17_SRAM (
  input  [16:0] Write_Data__16_0,
  input  Write_Select,
  input  Read_Select_1,
  input  Read_Select_2,
  input  Clock,
  output [16:0] Read_Data_1,
  output [16:0] Read_Data_2
);

  _1x1_SRAM u_1x1_sram_1 (
    .Write_Data(Write_Data__16_0[0]), .Write_Select(Write_Select), .Clock(Clock),
    .Read_Data_1(Read_Data_1[0]), .Read_Data_2(Read_Data_2[0]), .Read_Select_1(Read_Select_1),
    .Read_Select_2(Read_Select_2));
  _1x1_SRAM u_1x1_sram_2 (
    .Write_Data(Write_Data__16_0[4]), .Write_Select(Write_Select), .Clock(Clock),
    .Read_Data_1(Read_Data_1[4]), .Read_Data_2(Read_Data_2[4]), .Read_Select_1(Read_Select_1),
    .Read_Select_2(Read_Select_2));
  _1x1_SRAM u_1x1_sram_3 (
    .Write_Data(Write_Data__16_0[8]), .Write_Select(Write_Select), .Clock(Clock),
    .Read_Data_1(Read_Data_1[8]), .Read_Data_2(Read_Data_2[8]), .Read_Select_1(Read_Select_1),
    .Read_Select_2(Read_Select_2));
  _1x1_SRAM u_1x1_sram_4 (
    .Write_Data(Write_Data__16_0[12]), .Write_Select(Write_Select), .Clock(Clock),
    .Read_Data_1(Read_Data_1[12]), .Read_Data_2(Read_Data_2[12]), .Read_Select_1(Read_Select_1),
    .Read_Select_2(Read_Select_2));
  _1x1_SRAM u_1x1_sram_5 (
    .Write_Data(Write_Data__16_0[1]), .Write_Select(Write_Select), .Clock(Clock),
    .Read_Data_1(Read_Data_1[1]), .Read_Data_2(Read_Data_2[1]), .Read_Select_1(Read_Select_1),
    .Read_Select_2(Read_Select_2));
  _1x1_SRAM u_1x1_sram_6 (
    .Write_Data(Write_Data__16_0[5]), .Write_Select(Write_Select), .Clock(Clock),
    .Read_Data_1(Read_Data_1[5]), .Read_Data_2(Read_Data_2[5]), .Read_Select_1(Read_Select_1),
    .Read_Select_2(Read_Select_2));
  _1x1_SRAM u_1x1_sram_7 (
    .Write_Data(Write_Data__16_0[9]), .Write_Select(Write_Select), .Clock(Clock),
    .Read_Data_1(Read_Data_1[9]), .Read_Data_2(Read_Data_2[9]), .Read_Select_1(Read_Select_1),
    .Read_Select_2(Read_Select_2));
  _1x1_SRAM u_1x1_sram_8 (
    .Write_Data(Write_Data__16_0[13]), .Write_Select(Write_Select), .Clock(Clock),
    .Read_Data_1(Read_Data_1[13]), .Read_Data_2(Read_Data_2[13]), .Read_Select_1(Read_Select_1),
    .Read_Select_2(Read_Select_2));
  _1x1_SRAM u_1x1_sram_9 (
    .Write_Data(Write_Data__16_0[2]), .Write_Select(Write_Select), .Clock(Clock),
    .Read_Data_1(Read_Data_1[2]), .Read_Data_2(Read_Data_2[2]), .Read_Select_1(Read_Select_1),
    .Read_Select_2(Read_Select_2));
  _1x1_SRAM u_1x1_sram_10 (
    .Write_Data(Write_Data__16_0[6]), .Write_Select(Write_Select), .Clock(Clock),
    .Read_Data_1(Read_Data_1[6]), .Read_Data_2(Read_Data_2[6]), .Read_Select_1(Read_Select_1),
    .Read_Select_2(Read_Select_2));
  _1x1_SRAM u_1x1_sram_11 (
    .Write_Data(Write_Data__16_0[10]), .Write_Select(Write_Select), .Clock(Clock),
    .Read_Data_1(Read_Data_1[10]), .Read_Data_2(Read_Data_2[10]), .Read_Select_1(Read_Select_1),
    .Read_Select_2(Read_Select_2));
  _1x1_SRAM u_1x1_sram_12 (
    .Write_Data(Write_Data__16_0[14]), .Write_Select(Write_Select), .Clock(Clock),
    .Read_Data_1(Read_Data_1[14]), .Read_Data_2(Read_Data_2[14]), .Read_Select_1(Read_Select_1),
    .Read_Select_2(Read_Select_2));
  _1x1_SRAM u_1x1_sram_13 (
    .Write_Data(Write_Data__16_0[3]), .Write_Select(Write_Select), .Clock(Clock),
    .Read_Data_1(Read_Data_1[3]), .Read_Data_2(Read_Data_2[3]), .Read_Select_1(Read_Select_1),
    .Read_Select_2(Read_Select_2));
  _1x1_SRAM u_1x1_sram_14 (
    .Write_Data(Write_Data__16_0[7]), .Write_Select(Write_Select), .Clock(Clock),
    .Read_Data_1(Read_Data_1[7]), .Read_Data_2(Read_Data_2[7]), .Read_Select_1(Read_Select_1),
    .Read_Select_2(Read_Select_2));
  _1x1_SRAM u_1x1_sram_15 (
    .Write_Data(Write_Data__16_0[11]), .Write_Select(Write_Select), .Clock(Clock),
    .Read_Data_1(Read_Data_1[11]), .Read_Data_2(Read_Data_2[11]), .Read_Select_1(Read_Select_1),
    .Read_Select_2(Read_Select_2));
  _1x1_SRAM u_1x1_sram_16 (
    .Write_Data(Write_Data__16_0[15]), .Write_Select(Write_Select), .Clock(Clock),
    .Read_Data_1(Read_Data_1[15]), .Read_Data_2(Read_Data_2[15]), .Read_Select_1(Read_Select_1),
    .Read_Select_2(Read_Select_2));
  _1x1_SRAM u_1x1_sram_17 (
    .Write_Data(Write_Data__16_0[16]), .Write_Select(Write_Select), .Clock(Clock),
    .Read_Data_1(Read_Data_1[16]), .Read_Data_2(Read_Data_2[16]), .Read_Select_1(Read_Select_1),
    .Read_Select_2(Read_Select_2));

  // Other names for the same wires on the sheet: CLK = Clock; RD1_0 = Read_Data_1[0]; RD1_1 = Read_Data_1[1];
  //   RD1_2 = Read_Data_1[2]; RD1_3 = Read_Data_1[3]; RD1_4 = Read_Data_1[4]; RD1_5 = Read_Data_1[5];
  //   RD1_6 = Read_Data_1[6]; RD1_7 = Read_Data_1[7]; RD1_8 = Read_Data_1[8]; RD1_9 = Read_Data_1[9];
  //   RD1_10 = Read_Data_1[10]; RD1_11 = Read_Data_1[11]; RD1_12 = Read_Data_1[12]; RD1_13 = Read_Data_1[13];
  //   RD1_14 = Read_Data_1[14]; RD1_15 = Read_Data_1[15]; RD1_16 = Read_Data_1[16]; RD2_0 = Read_Data_2[0];
  //   RD2_1 = Read_Data_2[1]; RD2_2 = Read_Data_2[2]; RD2_3 = Read_Data_2[3]; RD2_4 = Read_Data_2[4];
  //   RD2_5 = Read_Data_2[5]; RD2_6 = Read_Data_2[6]; RD2_7 = Read_Data_2[7]; RD2_8 = Read_Data_2[8];
  //   RD2_9 = Read_Data_2[9]; RD2_10 = Read_Data_2[10]; RD2_11 = Read_Data_2[11]; RD2_12 = Read_Data_2[12];
  //   RD2_13 = Read_Data_2[13]; RD2_14 = Read_Data_2[14]; RD2_15 = Read_Data_2[15]; RD2_16 = Read_Data_2[16];
  //   RS1 = Read_Select_1; RS2 = Read_Select_2; D0 = Write_Data__16_0[0]; D1 = Write_Data__16_0[1];
  //   D2 = Write_Data__16_0[2]; D3 = Write_Data__16_0[3]; D4 = Write_Data__16_0[4]; D5 = Write_Data__16_0[5];
  //   D6 = Write_Data__16_0[6]; D7 = Write_Data__16_0[7]; D8 = Write_Data__16_0[8]; D9 = Write_Data__16_0[9];
  //   D10 = Write_Data__16_0[10]; D11 = Write_Data__16_0[11]; D12 = Write_Data__16_0[12]; D13 = Write_Data__16_0[13];
  //   D14 = Write_Data__16_0[14]; D15 = Write_Data__16_0[15]; D16 = Write_Data__16_0[16]; WS = Write_Select

  // Notes on the sheet:
  //   Roll: 1703057
endmodule

module _10x17_SRAM (
  input  [16:0] Write_Data__16_0,
  input  Clock,
  input  [3:0] Read_Address_1__3_0,
  input  [3:0] Read_Address_2__3_0,
  input  Write_Enable,
  input  [3:0] Write_Address__3_0,
  output [16:0] Read_Data_1__16_0,
  output [16:0] Read_Data_2__16_0
);

  wire R1_0, R1_1, R1_2, R1_3, R1_4, R1_5, R1_6, R1_7, R1_8, R1_9, R2_0, R2_1, R2_2, R2_3, R2_4, R2_5, R2_6,
       R2_7, R2_8, R2_9, W0, W1, W2, W3, W4, W5, W6, W7, W8, W9;
  wire [16:0] RD1_0, RD1_1, RD1_2, RD1_3, RD1_4, RD1_5, RD1_6, RD1_7, RD1_8, RD1_9, RD2_0, RD2_1, RD2_2,
       RD2_3, RD2_4, RD2_5, RD2_6, RD2_7, RD2_8, RD2_9;

  Decoder #(.select(4), .enable("false")) decoder_1 (
    .out0(R1_0), .out1(R1_1), .out2(R1_2), .out3(R1_3), .out4(R1_4), .out5(R1_5), .out6(R1_6), .out7(R1_7),
    .out8(R1_8), .out9(R1_9), .sel(Read_Address_1__3_0));  // open: out10, out11, out12, out13, out14, out15
  Decoder #(.select(4), .enable("false")) decoder_2 (
    .out0(R2_0), .out1(R2_1), .out2(R2_2), .out3(R2_3), .out4(R2_4), .out5(R2_5), .out6(R2_6), .out7(R2_7),
    .out8(R2_8), .out9(R2_9), .sel(Read_Address_2__3_0));  // open: out10, out11, out12, out13, out14, out15
  Decoder #(.select(4)) decoder_3 (
    .out0(W0), .out1(W1), .out2(W2), .out3(W3), .out4(W4), .out5(W5), .out6(W6), .out7(W7), .out8(W8),
    .out9(W9), .sel(Write_Address__3_0), .en(Write_Enable));  // open: out10, out11, out12, out13, out14, out15
  _1x17_SRAM u_1x17_sram_1 (
    .Write_Data__16_0(Write_Data__16_0), .Write_Select(W0), .Read_Select_1(R1_0), .Read_Select_2(R2_0),
    .Clock(Clock), .Read_Data_1(RD1_0), .Read_Data_2(RD2_0));
  _1x17_SRAM u_1x17_sram_2 (
    .Write_Data__16_0(Write_Data__16_0), .Write_Select(W1), .Read_Select_1(R1_1), .Read_Select_2(R2_1),
    .Clock(Clock), .Read_Data_1(RD1_1), .Read_Data_2(RD2_1));
  _1x17_SRAM u_1x17_sram_3 (
    .Write_Data__16_0(Write_Data__16_0), .Write_Select(W2), .Read_Select_1(R1_2), .Read_Select_2(R2_2),
    .Clock(Clock), .Read_Data_1(RD1_2), .Read_Data_2(RD2_2));
  _1x17_SRAM u_1x17_sram_4 (
    .Write_Data__16_0(Write_Data__16_0), .Write_Select(W3), .Read_Select_1(R1_3), .Read_Select_2(R2_3),
    .Clock(Clock), .Read_Data_1(RD1_3), .Read_Data_2(RD2_3));
  _1x17_SRAM u_1x17_sram_5 (
    .Write_Data__16_0(Write_Data__16_0), .Write_Select(W4), .Read_Select_1(R1_4), .Read_Select_2(R2_4),
    .Clock(Clock), .Read_Data_1(RD1_4), .Read_Data_2(RD2_4));
  _1x17_SRAM u_1x17_sram_6 (
    .Write_Data__16_0(Write_Data__16_0), .Write_Select(W5), .Read_Select_1(R1_5), .Read_Select_2(R2_5),
    .Clock(Clock), .Read_Data_1(RD1_5), .Read_Data_2(RD2_5));
  _1x17_SRAM u_1x17_sram_7 (
    .Write_Data__16_0(Write_Data__16_0), .Write_Select(W6), .Read_Select_1(R1_6), .Read_Select_2(R2_6),
    .Clock(Clock), .Read_Data_1(RD1_6), .Read_Data_2(RD2_6));
  _1x17_SRAM u_1x17_sram_8 (
    .Write_Data__16_0(Write_Data__16_0), .Write_Select(W7), .Read_Select_1(R1_7), .Read_Select_2(R2_7),
    .Clock(Clock), .Read_Data_1(RD1_7), .Read_Data_2(RD2_7));
  _1x17_SRAM u_1x17_sram_9 (
    .Write_Data__16_0(Write_Data__16_0), .Write_Select(W8), .Read_Select_1(R1_8), .Read_Select_2(R2_8),
    .Clock(Clock), .Read_Data_1(RD1_8), .Read_Data_2(RD2_8));
  _1x17_SRAM u_1x17_sram_10 (
    .Write_Data__16_0(Write_Data__16_0), .Write_Select(W9), .Read_Select_1(R1_9), .Read_Select_2(R2_9),
    .Clock(Clock), .Read_Data_1(RD1_9), .Read_Data_2(RD2_9));
  assign Read_Data_1__16_0 = RD1_0 | RD1_1 | RD1_2 | RD1_3 | RD1_4 | RD1_5 | RD1_6 | RD1_7 | RD1_8 | RD1_9;  // OR_Gate or_1, 17 bits wide
  assign Read_Data_2__16_0 = RD2_0 | RD2_1 | RD2_2 | RD2_3 | RD2_4 | RD2_5 | RD2_6 | RD2_7 | RD2_8 | RD2_9;  // OR_Gate or_2, 17 bits wide

  // Notes on the sheet:
  //   Roll: 1703057
endmodule

module _4_bit_Counter_Register (
  input  [3:0] Din_3_0,
  input  Clock,
  output [3:0] Dout_3_0
);

  // Register_Set_Library_1_bit_Register 1_bit_register_1: pin names not known; wires that end beside it: Din_3_0[0], 1'b1, Clock, Dout_3_0[0]
  // Register_Set_Library_1_bit_Register 1_bit_register_2: pin names not known; wires that end beside it: Din_3_0[1], 1'b1, Clock, Dout_3_0[1]
  // Register_Set_Library_1_bit_Register 1_bit_register_3: pin names not known; wires that end beside it: Din_3_0[2], 1'b1, Clock, Dout_3_0[2]
  // Register_Set_Library_1_bit_Register 1_bit_register_4: pin names not known; wires that end beside it: Din_3_0[3], 1'b1, Clock, Dout_3_0[3]

  // Notes on the sheet:
  //   Roll: 1703057
endmodule

module _4_bit_PC_Adder (
  input  [3:0] I__3_0,
  output [3:0] O__3_0
);

  wire [3:0] bit_extender_1_out;

  assign bit_extender_1_out = {{3{1'b0}}, 1'b1};  // Bit_Extender bit_extender_1
  Adder #(.width(4)) adder_1 (.a(I__3_0), .b(bit_extender_1_out), .out(O__3_0));  // open: cin, cout

  // Notes on the sheet:
  //   Roll: 1703057
endmodule

module Control_Unit (
  input  [2:0] Opcode__2_0,
  input  CF,
  output Op,
  output Imm_Sel,
  output WE,
  output Jmp_Sel
);

  wire Branch_out, JC_out, not_1_out, not_2_out, not_3_out, not_4_out, not_5_out, Reg_out;

  not not_1 (not_1_out, Opcode__2_0[0]);
  not not_2 (not_2_out, Opcode__2_0[2]);
  and Imm (Imm_Sel, not_2_out, Opcode__2_0[1]);
  not not_3 (not_3_out, Opcode__2_0[2]);
  and Reg (Reg_out, not_3_out, not_4_out);
  not not_4 (not_4_out, Opcode__2_0[1]);
  and Branch (Branch_out, Opcode__2_0[2], not_5_out);
  not not_5 (not_5_out, Opcode__2_0[1]);
  and JC (JC_out, Branch_out, not_1_out);
  or or_1 (WE, Imm_Sel, Reg_out);
  and and_1 (Jmp_Sel, JC_out, CF);

  assign Op = Opcode__2_0[0];

  // Notes on the sheet:
  //   To check if JC is working
  //   Roll: 1703057
endmodule

module Flag_Register (
  input  CFin,
  input  SFin,
  input  ZFin,
  input  Clock,
  output CFout,
  output SFout,
  output ZFout
);

  _1_bit_Register u_1_bit_register_1 (.Din(CFin), .Sel(1'b1), .Dout(CFout), .Clock(Clock));
  _1_bit_Register u_1_bit_register_2 (.Din(SFin), .Sel(1'b1), .Dout(SFout), .Clock(Clock));
  _1_bit_Register u_1_bit_register_3 (.Din(ZFin), .Sel(1'b1), .Dout(ZFout), .Clock(Clock));

  // Notes on the sheet:
  //   Roll: 1703057
endmodule

// 1
module CPU (
  input  [3:0] Write_Address__3_0,
  input  [16:0] Write_Data__16_0,
  input  [2:0] in_3,
  input  Write_Enable,
  input  [4:0] in_5,
  input  Clock,
  input  CPU_Enable,
  output [16:0] out_8
);

  wire alu_1_cf, alu_1_sf, alu_1_zf, CF, CPU_CLK, Imm_Sel, Jmp_Sel, OP, WE;
  wire [3:0] multiplexer_1_out, n4_bit_counter_register_1_dout_3_0, n4_bit_pc_adder_1_o__3_0;
  wire [4:0] alu_1_r__4_0, multiplexer_2_out, register_set_with_5_5_bit_registers_1_a,
       register_set_with_5_5_bit_registers_1_b;

  _4_bit_PC_Adder u_4_bit_pc_adder_1 (.I__3_0(n4_bit_counter_register_1_dout_3_0), .O__3_0(n4_bit_pc_adder_1_o__3_0));
  Multiplexer #(.width(4), .enable("false")) multiplexer_1 (
    .in0(n4_bit_pc_adder_1_o__3_0), .in1(out_8[13:10]), .out(multiplexer_1_out), .sel(Jmp_Sel));
  _4_bit_Counter_Register u_4_bit_counter_register_1 (
    .Din_3_0(multiplexer_1_out), .Clock(CPU_CLK), .Dout_3_0(n4_bit_counter_register_1_dout_3_0));
  and and_1 (CPU_CLK, Clock, CPU_Enable);
  _10x17_SRAM u_10x17_sram_1 (
    .Write_Data__16_0(Write_Data__16_0), .Clock(Clock),
    .Read_Address_1__3_0(n4_bit_counter_register_1_dout_3_0), .Write_Enable(Write_Enable),
    .Write_Address__3_0(Write_Address__3_0), .Read_Data_1__16_0(out_8));  // open: Read_Address_2__3_0, Read_Data_2__16_0
  Control_Unit control_unit_1 (
    .Opcode__2_0(out_8[16:14]), .Op(OP), .Imm_Sel(Imm_Sel), .WE(WE), .CF(CF), .Jmp_Sel(Jmp_Sel));
  Register_Set_with_5_5_bit_Registers register_set_with_5_5_bit_registers_1 (
    .WE(WE), .Wr(out_8[13:11]), .Wrd(alu_1_r__4_0), .Clock(Clock), .Ra(out_8[13:11]), .Rb(out_8[10:8]),
    .A(register_set_with_5_5_bit_registers_1_a), .B(register_set_with_5_5_bit_registers_1_b));
  Multiplexer #(.width(5), .enable("false")) multiplexer_2 (
    .in0(register_set_with_5_5_bit_registers_1_b), .in1(out_8[10:6]), .out(multiplexer_2_out), .sel(Imm_Sel));
  ALU alu_1 (
    .A__4_0(register_set_with_5_5_bit_registers_1_a), .B_4_0(multiplexer_2_out), .OP(OP),
    .R__4_0(alu_1_r__4_0), .CF(alu_1_cf), .SF(alu_1_sf), .ZF(alu_1_zf));
  Flag_Register flag_register_1 (
    .CFin(alu_1_cf), .SFin(alu_1_sf), .ZFin(alu_1_zf), .Clock(CPU_CLK), .CFout(CF));  // open: SFout, ZFout

  // Other names for the same wires on the sheet: CLK = Clock

  // Notes on the sheet:
  //   Register Mode OR = 00010001100000000
  //   Branching Mode JC = 100 0010 0000000000
  //   Immediate Mode OR = 01010011000000000
  //   Roll: 1703057
  //   Branching Mode: Opcode (2bit + 1 bit) + Address (4 bit) + Unused (10 bit) ----> Opcode 1st 2 bit = 10 + Opcode last 1 bit = JC (0)
  //   Register Mode: Opcode (2bit + 1 bit) + Register RA (3 bit) + Register RB (3 bit) + Unused (8 bit) ----> Opcode 1st 2 bit = 00 + Opcode last 1 bit = OR (0), SHR (1)
  //   Immediate Mode: Opcode (2bit + 1 bit) + Register RA (3 bit) + Immediate Value (5 bit) + Unused (6 bit) ----> Opcode 1st 2 bit = 01 + Opcode last 1 bit =  OR (0), SHR (1)
  //   Connect with 'CLK' =  just to store
  //   'CPU_CLK' = To star PC
  //   To see the instructions easily
  //   max address is 100
  //   Register Mode SHR = 00100000100000000
  //   Immediate Mode SHR = 01100010011000000
  //   (Jump to the 2nd instruction if JC=1. But it will never be executed because in OR or SHR operations, JC will never be active)
  //   to write manually
endmodule
